// Logisim project IC_Lab_4.circ as structural Verilog: 1 circuit, main circuit main
module main (
  input  Reset,
  input  Up_Down,
  input  _1
);

  wire clock_1_out, n7404_1_pin2, n7408_1_pin1, n7408_1_pin3, n7408_1_pin5, n7408_1_pin6, n7408_1_pin9,
       n7408_1_pin10, n7408_1_pin12, n7408_1_pin13, n7432_1_pin11, n7486_1_pin3, n7486_1_pin5, n7486_1_pin6,
       n7486_1_pin8, n7486_1_pin11;

  Clock clock_1 (.out(clock_1_out));
  _7404 u_7404_1 (
    .pin1(Up_Down), .pin2(n7404_1_pin2));  // open: pin3, pin4, pin5, pin6, pin13, pin12, pin11, pin10, pin9, pin8
  _7408 u_7408_1 (
    .pin1(n7408_1_pin1), .pin2(n7404_1_pin2), .pin3(n7408_1_pin3), .pin4(Up_Down), .pin5(n7408_1_pin5),
    .pin6(n7408_1_pin6), .pin13(n7408_1_pin13), .pin12(n7408_1_pin12), .pin11(n7408_1_pin1),
    .pin10(n7408_1_pin10), .pin9(n7408_1_pin9), .pin8(n7408_1_pin5));
  _7432 u_7432_1 (
    .pin13(n7408_1_pin6), .pin12(n7408_1_pin3), .pin11(n7432_1_pin11));  // open: pin1, pin2, pin3, pin4, pin5, pin6, pin10, pin9, pin8
  _7486 u_7486_1 (
    .pin1(Up_Down), .pin2(n7408_1_pin12), .pin3(n7486_1_pin3), .pin4(n7432_1_pin11), .pin5(n7486_1_pin5),
    .pin6(n7486_1_pin6), .pin13(_1), .pin12(n7408_1_pin12), .pin11(n7486_1_pin11), .pin10(n7486_1_pin3),
    .pin9(n7408_1_pin13), .pin8(n7486_1_pin8));
  LED S3 (.in(n7486_1_pin5));
  LED S2 (.in(n7408_1_pin13));
  _7474 u_7474_1 (
    .pin1(Reset), .pin2(n7486_1_pin11), .pin3(clock_1_out), .pin5(n7408_1_pin12), .pin6(n7408_1_pin10),
    .pin13(Reset), .pin12(n7486_1_pin8), .pin11(clock_1_out), .pin9(n7408_1_pin13), .pin8(n7408_1_pin9));  // open: pin4, pin10
  _7474 u_7474_2 (
    .pin13(Reset), .pin12(n7486_1_pin6), .pin11(clock_1_out), .pin9(n7486_1_pin5));  // open: pin1, pin2, pin3, pin4, pin5, pin6, pin10, pin8
  LED S1 (.in(n7408_1_pin12));
endmodule
