// Logisim project Lab_3.circ as structural Verilog: 1 circuit, main circuit main
module main (
  input  _0,
  input  B3,
  input  B2,
  input  B1,
  input  A1,
  input  A2,
  input  A3,
  output [5:0] out_8
);

  wire [1:0] and_8_out;
  wire [2:0] adder_2_cout, and_4_out, and_7_out;

  and and_1 (and_4_out[2], A3, B3);
  and and_2 (and_4_out[1], A3, B2);
  and and_3 (and_7_out[2], A2, B3);
  and and_4 (and_4_out[0], A3, B1);
  and and_5 (and_7_out[1], A2, B2);
  LED S6 (.in(out_8[5]));
  and and_6 (and_8_out[1], A1, B3);
  and and_7 (and_7_out[0], A2, B1);
  LED S5 (.in(out_8[4]));
  LED S4 (.in(out_8[3]));
  and and_8 (and_8_out[0], A1, B2);
  Adder #(.width(3)) adder_1 (.a(adder_2_cout), .b(and_4_out), .out(out_8[4:2]), .cout(out_8[5]));  // open: cin
  LED S3 (.in(out_8[2]));
  LED S2 (.in(out_8[1]));
  and and_9 (out_8[0], A1, B1);
  Adder #(.width(3)) adder_2 (
    .a({_0, and_8_out}), .b(and_7_out), .out({adder_2_cout[1:0], out_8[1]}), .cout(adder_2_cout[2]));  // open: cin
  LED S1 (.in(out_8[0]));

  // Notes on the sheet:
  //   MD Rokib Hasan Oli
  //   2211950642
  //   Group-6
endmodule
