// Logisim project Lab_4.circ as structural Verilog: 1 circuit, main circuit main
module main (
  input  RESET,
  input  in_2,
  input  M,
  output [2:0] out_4
);

  wire and_1_out, and_2_out, and_3_out, and_4_out, clock_1_out, not_1_out, or_1_out, TA_qn, TB_qn, xor_1_out,
       xor_2_out, xor_3_out, xor_4_out;

  not not_1 (not_1_out, M);
  and and_1 (and_1_out, TB_qn, TA_qn);
  and and_2 (and_2_out, out_4[0], out_4[1]);
  and and_3 (and_3_out, and_1_out, M);
  and and_4 (and_4_out, not_1_out, and_2_out);
  or or_1 (or_1_out, and_3_out, and_4_out);
  xor xor_1 (xor_1_out, out_4[0], M);
  xor xor_2 (xor_2_out, out_4[1], xor_1_out);
  D_Flip_Flop TC (.D(xor_3_out), .clk(clock_1_out), .Q(out_4[2]), .reset(RESET));  // open: Qn, preset
  xor xor_3 (xor_3_out, out_4[2], or_1_out);
  Clock clock_1 (.out(clock_1_out));
  D_Flip_Flop TA (.D(xor_4_out), .clk(clock_1_out), .Q(out_4[0]), .Qn(TA_qn), .reset(RESET));  // open: preset
  xor xor_4 (xor_4_out, out_4[0], in_2);
  D_Flip_Flop TB (.D(xor_2_out), .clk(clock_1_out), .Q(out_4[1]), .Qn(TB_qn), .reset(RESET));  // open: preset
  LED led_1 (.in(out_4[2]));
  LED led_2 (.in(out_4[1]));
  LED led_3 (.in(out_4[0]));

  // Notes on the sheet:
  //   MD Rokib Hasan Oli
  //   2211950642
  //   Group-6
endmodule
