// Logisim project Lab_6.circ as structural Verilog
module Registers (
  input  [3:0] Read_Register_1_RS,
  input  [3:0] Read_Register_2_RT,
  input  [3:0] Write_Register_RD,
  input  [15:0] Write_Data,
  input  RegWrite,
  input  Clock,
  output [15:0] Read_Data_1,
  output [15:0] Read_Data_2
);

  wire and_1_out, and_2_out, and_3_out, and_4_out, and_5_out, and_6_out, and_7_out, and_8_out, and_9_out,
       and_10_out, and_11_out, and_12_out, and_13_out, and_14_out, and_15_out, and_16_out, decoder_1_out0,
       decoder_1_out1, decoder_1_out2, decoder_1_out3, decoder_1_out4, decoder_1_out5, decoder_1_out6,
       decoder_1_out7, decoder_1_out8, decoder_1_out9, decoder_1_out10, decoder_1_out11, decoder_1_out12,
       decoder_1_out13, decoder_1_out14, decoder_1_out15;
  wire [15:0] R_1_q, R_2_q, R_3_q, R_4_q, R_5_q, R_6_q, R_7_q, R_8_q, R_9_q, R_10_q, R_11_q, R_12_q, R_13_q,
       R_14_q, R_15_q, R_16_q;

  Decoder #(.select(4)) decoder_1 (
    .out0(decoder_1_out0), .out1(decoder_1_out1), .out2(decoder_1_out2), .out3(decoder_1_out3),
    .out4(decoder_1_out4), .out5(decoder_1_out5), .out6(decoder_1_out6), .out7(decoder_1_out7),
    .out8(decoder_1_out8), .out9(decoder_1_out9), .out10(decoder_1_out10), .out11(decoder_1_out11),
    .out12(decoder_1_out12), .out13(decoder_1_out13), .out14(decoder_1_out14), .out15(decoder_1_out15),
    .sel(Write_Register_RD));  // open: en
  and and_1 (and_1_out, decoder_1_out0, RegWrite);
  and and_2 (and_2_out, decoder_1_out1, RegWrite);
  and and_3 (and_3_out, decoder_1_out2, RegWrite);
  and and_4 (and_4_out, decoder_1_out3, RegWrite);
  and and_5 (and_5_out, decoder_1_out4, RegWrite);
  and and_6 (and_6_out, decoder_1_out5, RegWrite);
  and and_7 (and_7_out, decoder_1_out6, RegWrite);
  and and_8 (and_8_out, decoder_1_out7, RegWrite);
  and and_9 (and_9_out, decoder_1_out8, RegWrite);
  and and_10 (and_10_out, decoder_1_out9, RegWrite);
  and and_11 (and_11_out, decoder_1_out10, RegWrite);
  and and_12 (and_12_out, decoder_1_out11, RegWrite);
  and and_13 (and_13_out, decoder_1_out12, RegWrite);
  and and_14 (and_14_out, decoder_1_out13, RegWrite);
  and and_15 (and_15_out, decoder_1_out14, RegWrite);
  and and_16 (and_16_out, decoder_1_out15, RegWrite);
  Register #(.width(16)) R_1 (.D(Write_Data), .en(and_1_out), .clk(Clock), .Q(R_1_q));  // open: clr
  Register #(.width(16)) R_2 (.D(Write_Data), .en(and_2_out), .clk(Clock), .Q(R_2_q));  // open: clr
  Register #(.width(16)) R_3 (.D(Write_Data), .en(and_3_out), .clk(Clock), .Q(R_3_q));  // open: clr
  Register #(.width(16)) R_4 (.D(Write_Data), .en(and_4_out), .clk(Clock), .Q(R_4_q));  // open: clr
  Register #(.width(16)) R_5 (.D(Write_Data), .en(and_5_out), .clk(Clock), .Q(R_5_q));  // open: clr
  Register #(.width(16)) R_6 (.D(Write_Data), .en(and_6_out), .clk(Clock), .Q(R_6_q));  // open: clr
  Register #(.width(16)) R_7 (.D(Write_Data), .en(and_7_out), .clk(Clock), .Q(R_7_q));  // open: clr
  Register #(.width(16)) R_8 (.D(Write_Data), .en(and_8_out), .clk(Clock), .Q(R_8_q));  // open: clr
  Register #(.width(16)) R_9 (.D(Write_Data), .en(and_9_out), .clk(Clock), .Q(R_9_q));  // open: clr
  Register #(.width(16)) R_10 (.D(Write_Data), .en(and_10_out), .clk(Clock), .Q(R_10_q));  // open: clr
  Register #(.width(16)) R_11 (.D(Write_Data), .en(and_11_out), .clk(Clock), .Q(R_11_q));  // open: clr
  Register #(.width(16)) R_12 (.D(Write_Data), .en(and_12_out), .clk(Clock), .Q(R_12_q));  // open: clr
  Register #(.width(16)) R_13 (.D(Write_Data), .en(and_13_out), .clk(Clock), .Q(R_13_q));  // open: clr
  Register #(.width(16)) R_14 (.D(Write_Data), .en(and_14_out), .clk(Clock), .Q(R_14_q));  // open: clr
  Register #(.width(16)) R_15 (.D(Write_Data), .en(and_15_out), .clk(Clock), .Q(R_15_q));  // open: clr
  Register #(.width(16)) R_16 (.D(Write_Data), .en(and_16_out), .clk(Clock), .Q(R_16_q));  // open: clr
  Multiplexer #(.select(4), .width(16)) multiplexer_1 (
    .in0(R_1_q), .in1(R_2_q), .in2(R_3_q), .in3(R_4_q), .in4(R_5_q), .in5(R_6_q), .in6(R_7_q), .in7(R_8_q),
    .in8(R_9_q), .in9(R_10_q), .in10(R_11_q), .in11(R_12_q), .in12(R_13_q), .in13(R_14_q), .in14(R_15_q),
    .in15(R_16_q), .out(Read_Data_1), .sel(Read_Register_1_RS));
  Multiplexer #(.select(4), .width(16)) multiplexer_2 (
    .in0(R_1_q), .in1(R_2_q), .in2(R_3_q), .in3(R_4_q), .in4(R_5_q), .in5(R_6_q), .in6(R_7_q), .in7(R_8_q),
    .in8(R_9_q), .in9(R_10_q), .in10(R_11_q), .in11(R_12_q), .in12(R_13_q), .in13(R_14_q), .in14(R_15_q),
    .in15(R_16_q), .out(Read_Data_2), .sel(Read_Register_2_RT));

  // Notes on the sheet:
  //   RS=RT=RT=2,2^4=16;16 Registers in a Register File, Data Bits=16(ALU 16 Bits)
endmodule

module ALU (
  input  Cin,
  input  A,
  input  B,
  input  [1:0] SelectMUX,
  output Result,
  output Cout
);

  wire adder_1_out, and_1_out, and_2_out, multiplexer_1_out, not_1_out, or_1_out;

  Multiplexer multiplexer_1 (.in0(B), .in1(not_1_out), .out(multiplexer_1_out), .sel(and_2_out));
  not not_1 (not_1_out, B);
  Adder #(.width(1)) adder_1 (.a(A), .b(multiplexer_1_out), .out(adder_1_out), .cin(Cin), .cout(Cout));
  and and_1 (and_1_out, A, B);
  or or_1 (or_1_out, A, B);
  and and_2 (and_2_out, SelectMUX[0], SelectMUX[1]);
  Multiplexer #(.select(2)) multiplexer_2 (
    .in0(and_1_out), .in1(or_1_out), .in2(adder_1_out), .in3(adder_1_out), .out(Result), .sel(SelectMUX));
endmodule

module SixteenBitALU (
  input  [1:0] SelectMUX,
  input  Cin,
  input  [15:0] A,
  input  [15:0] B,
  output [15:0] Result,
  output Cout
);

  wire Eight_cout, Eleven_cout, Fifteen_cout, Five_cout, Four_cout, Fourteen_cout, Nine_cout, One_cout,
       Seven_cout, Six_cout, Ten_cout, Thirteen_cout, Three_cout, Twelve_cout, Two_cout;

  ALU One (.Cin(Cin), .A(A[0]), .B(B[0]), .SelectMUX(SelectMUX), .Result(Result[0]), .Cout(One_cout));
  ALU Two (.Cin(One_cout), .A(A[1]), .B(B[1]), .SelectMUX(SelectMUX), .Result(Result[1]), .Cout(Two_cout));
  ALU Three (.Cin(Two_cout), .A(A[2]), .B(B[2]), .SelectMUX(SelectMUX), .Result(Result[2]), .Cout(Three_cout));
  ALU Four (.Cin(Three_cout), .A(A[3]), .B(B[3]), .SelectMUX(SelectMUX), .Result(Result[3]), .Cout(Four_cout));
  ALU Five (.Cin(Four_cout), .A(A[4]), .B(B[4]), .SelectMUX(SelectMUX), .Result(Result[4]), .Cout(Five_cout));
  ALU Six (.Cin(Five_cout), .A(A[5]), .B(B[5]), .SelectMUX(SelectMUX), .Result(Result[5]), .Cout(Six_cout));
  ALU Seven (.Cin(Six_cout), .A(A[6]), .B(B[6]), .SelectMUX(SelectMUX), .Result(Result[6]), .Cout(Seven_cout));
  ALU Eight (.Cin(Seven_cout), .A(A[7]), .B(B[7]), .SelectMUX(SelectMUX), .Result(Result[7]), .Cout(Eight_cout));
  ALU Nine (.Cin(Eight_cout), .A(A[8]), .B(B[8]), .SelectMUX(SelectMUX), .Result(Result[8]), .Cout(Nine_cout));
  ALU Ten (.Cin(Nine_cout), .A(A[9]), .B(B[9]), .SelectMUX(SelectMUX), .Result(Result[9]), .Cout(Ten_cout));
  ALU Eleven (.Cin(Ten_cout), .A(A[10]), .B(B[10]), .SelectMUX(SelectMUX), .Result(Result[10]), .Cout(Eleven_cout));
  ALU Twelve (.Cin(Eleven_cout), .A(A[11]), .B(B[11]), .SelectMUX(SelectMUX), .Result(Result[11]), .Cout(Twelve_cout));
  ALU Thirteen (
    .Cin(Twelve_cout), .A(A[12]), .B(B[12]), .SelectMUX(SelectMUX), .Result(Result[12]), .Cout(Thirteen_cout));
  ALU Fourteen (
    .Cin(Thirteen_cout), .A(A[13]), .B(B[13]), .SelectMUX(SelectMUX), .Result(Result[13]),
    .Cout(Fourteen_cout));
  ALU Fifteen (
    .Cin(Fourteen_cout), .A(A[14]), .B(B[14]), .SelectMUX(SelectMUX), .Result(Result[14]), .Cout(Fifteen_cout));
  ALU Sixteen (.Cin(Fifteen_cout), .A(A[15]), .B(B[15]), .SelectMUX(SelectMUX), .Result(Result[15]), .Cout(Cout));

  // Notes on the sheet:
  //   16-Bit ALU
  //   2211950642
  //   Group-6
  //   MD. Rokib Hasan Oli
endmodule
