// Logisim project Lab_8.circ as structural Verilog
module Register (
  input  [3:0] Read_Register_1_RS,
  input  [3:0] Read_Register_2_RT,
  input  [3:0] Write_Register_RD,
  input  [15:0] Write_Data,
  input  RegWrite,
  input  Clock,
  output [15:0] Read_Data_1,
  output [15:0] Read_Data_2
);

  wire and_1_out, and_2_out, and_3_out, and_4_out, and_5_out, and_6_out, and_7_out, and_8_out, and_9_out,
       and_10_out, and_11_out, and_12_out, and_13_out, and_14_out, and_15_out, and_16_out, decoder_1_out0,
       decoder_1_out1, decoder_1_out2, decoder_1_out3, decoder_1_out4, decoder_1_out5, decoder_1_out6,
       decoder_1_out7, decoder_1_out8, decoder_1_out9, decoder_1_out10, decoder_1_out11, decoder_1_out12,
       decoder_1_out13, decoder_1_out14, decoder_1_out15;
  wire [15:0] _1_q, _2_q, _3_q, _4_q, _5_q, _6_q, _7_q, _8_q, _9_q, _10_q, _11_q, _12_q, _13_q, _14_q, _15_q,
       _16_q;

  Decoder #(.select(4)) decoder_1 (
    .out0(decoder_1_out0), .out1(decoder_1_out1), .out2(decoder_1_out2), .out3(decoder_1_out3),
    .out4(decoder_1_out4), .out5(decoder_1_out5), .out6(decoder_1_out6), .out7(decoder_1_out7),
    .out8(decoder_1_out8), .out9(decoder_1_out9), .out10(decoder_1_out10), .out11(decoder_1_out11),
    .out12(decoder_1_out12), .out13(decoder_1_out13), .out14(decoder_1_out14), .out15(decoder_1_out15),
    .sel(Write_Register_RD));  // open: en
  and and_1 (and_1_out, decoder_1_out0, RegWrite);
  and and_2 (and_2_out, decoder_1_out1, RegWrite);
  and and_3 (and_3_out, decoder_1_out2, RegWrite);
  and and_4 (and_4_out, decoder_1_out3, RegWrite);
  and and_5 (and_5_out, decoder_1_out4, RegWrite);
  and and_6 (and_6_out, decoder_1_out5, RegWrite);
  and and_7 (and_7_out, decoder_1_out6, RegWrite);
  and and_8 (and_8_out, decoder_1_out7, RegWrite);
  and and_9 (and_9_out, decoder_1_out8, RegWrite);
  and and_10 (and_10_out, decoder_1_out9, RegWrite);
  and and_11 (and_11_out, decoder_1_out10, RegWrite);
  and and_12 (and_12_out, decoder_1_out11, RegWrite);
  and and_13 (and_13_out, decoder_1_out12, RegWrite);
  and and_14 (and_14_out, decoder_1_out13, RegWrite);
  and and_15 (and_15_out, decoder_1_out14, RegWrite);
  and and_16 (and_16_out, decoder_1_out15, RegWrite);
  Register_part #(.width(16)) _1 (.D(Write_Data), .en(and_1_out), .Q(_1_q), .clk(Clock));  // open: clr
  Register_part #(.width(16)) _2 (.D(Write_Data), .en(and_2_out), .Q(_2_q), .clk(Clock));  // open: clr
  Register_part #(.width(16)) _3 (.D(Write_Data), .en(and_3_out), .Q(_3_q), .clk(Clock));  // open: clr
  Register_part #(.width(16)) _4 (.D(Write_Data), .en(and_4_out), .Q(_4_q), .clk(Clock));  // open: clr
  Register_part #(.width(16)) _5 (.D(Write_Data), .en(and_5_out), .Q(_5_q), .clk(Clock));  // open: clr
  Register_part #(.width(16)) _6 (.D(Write_Data), .en(and_6_out), .Q(_6_q), .clk(Clock));  // open: clr
  Register_part #(.width(16)) _7 (.D(Write_Data), .en(and_7_out), .Q(_7_q), .clk(Clock));  // open: clr
  Register_part #(.width(16)) _8 (.D(Write_Data), .en(and_8_out), .Q(_8_q), .clk(Clock));  // open: clr
  Register_part #(.width(16)) _9 (.D(Write_Data), .en(and_9_out), .Q(_9_q), .clk(Clock));  // open: clr
  Register_part #(.width(16)) _10 (.D(Write_Data), .en(and_10_out), .Q(_10_q), .clk(Clock));  // open: clr
  Register_part #(.width(16)) _11 (.D(Write_Data), .en(and_11_out), .Q(_11_q), .clk(Clock));  // open: clr
  Register_part #(.width(16)) _12 (.D(Write_Data), .en(and_12_out), .Q(_12_q), .clk(Clock));  // open: clr
  Register_part #(.width(16)) _13 (.D(Write_Data), .en(and_13_out), .Q(_13_q), .clk(Clock));  // open: clr
  Register_part #(.width(16)) _14 (.D(Write_Data), .en(and_14_out), .Q(_14_q), .clk(Clock));  // open: clr
  Register_part #(.width(16)) _15 (.D(Write_Data), .en(and_15_out), .Q(_15_q), .clk(Clock));  // open: clr
  Register_part #(.width(16)) _16 (.D(Write_Data), .en(and_16_out), .Q(_16_q), .clk(Clock));  // open: clr
  Multiplexer #(.select(4), .width(16)) multiplexer_1 (
    .in0(_1_q), .in1(_2_q), .in2(_3_q), .in3(_4_q), .in4(_5_q), .in5(_6_q), .in6(_7_q), .in7(_8_q),
    .in8(_9_q), .in9(_10_q), .in10(_11_q), .in11(_12_q), .in12(_13_q), .in13(_14_q), .in14(_15_q),
    .in15(_16_q), .out(Read_Data_1), .sel(Read_Register_1_RS));  // open: en
  Multiplexer #(.select(4), .width(16)) multiplexer_2 (
    .in0(_1_q), .in1(_2_q), .in2(_3_q), .in3(_4_q), .in4(_5_q), .in5(_6_q), .in6(_7_q), .in7(_8_q),
    .in8(_9_q), .in9(_10_q), .in10(_11_q), .in11(_12_q), .in12(_13_q), .in13(_14_q), .in14(_15_q),
    .in15(_16_q), .out(Read_Data_2), .sel(Read_Register_2_RT));  // open: en

  // Notes on the sheet:
  //   rs=rt=rd=2^2=4;4 registers in a Register File, Data Bits=16(ALU 16 bits)
  //   $v0
  //   $v1
  //   $a0
  //   $a2
  //   $t0
  //   $t1
  //   $t2
  //   $t3
  //   $t4
  //   $s0
  //   $s2
  //   $s3
  //   $s4
  //   $zero
  //   $a1
  //   $s1
endmodule

module _1_Bit_ALU (
  input  A,
  input  B,
  input  [1:0] Select,
  input  Cin,
  output Result,
  output Cout
);

  wire adder_1_out, and_1_out, and_2_out, multiplexer_1_out, not_1_out, or_1_out;

  not not_1 (not_1_out, B);
  Multiplexer multiplexer_1 (.in0(B), .in1(not_1_out), .out(multiplexer_1_out), .sel(and_2_out));  // open: en
  and and_1 (and_1_out, A, B);
  or or_1 (or_1_out, A, B);
  Adder #(.width(1)) adder_1 (.a(A), .b(multiplexer_1_out), .out(adder_1_out), .cin(Cin), .cout(Cout));
  and and_2 (and_2_out, Select[0], Select[1]);
  Multiplexer #(.select(2)) multiplexer_2 (
    .in0(and_1_out), .in1(or_1_out), .in2(adder_1_out), .in3(adder_1_out), .out(Result), .sel(Select));  // open: en

  // Notes on the sheet:
  //   00 AND, 01 OR, 10 ADD, 11 SUB 
endmodule

module _16_Bit_ALU (
  input  Cin,
  input  [1:0] Select,
  input  [15:0] A,
  input  [15:0] B,
  output [15:0] Result,
  output Cout
);

  wire n1_bit_alu_1_cout, n1_bit_alu_2_cout, n1_bit_alu_3_cout, n1_bit_alu_4_cout, n1_bit_alu_5_cout,
       n1_bit_alu_6_cout, n1_bit_alu_7_cout, n1_bit_alu_8_cout, n1_bit_alu_9_cout, n1_bit_alu_10_cout,
       n1_bit_alu_11_cout, n1_bit_alu_12_cout, n1_bit_alu_13_cout, n1_bit_alu_14_cout, n1_bit_alu_15_cout;

  _1_Bit_ALU u_1_bit_alu_1 (
    .A(A[0]), .B(B[0]), .Select(Select), .Cin(Cin), .Result(Result[0]), .Cout(n1_bit_alu_1_cout));
  _1_Bit_ALU u_1_bit_alu_2 (
    .A(A[1]), .B(B[1]), .Select(Select), .Cin(n1_bit_alu_1_cout), .Result(Result[1]), .Cout(n1_bit_alu_2_cout));
  _1_Bit_ALU u_1_bit_alu_3 (
    .A(A[2]), .B(B[2]), .Select(Select), .Cin(n1_bit_alu_2_cout), .Result(Result[2]), .Cout(n1_bit_alu_3_cout));
  _1_Bit_ALU u_1_bit_alu_4 (
    .A(A[3]), .B(B[3]), .Select(Select), .Cin(n1_bit_alu_3_cout), .Result(Result[3]), .Cout(n1_bit_alu_4_cout));
  _1_Bit_ALU u_1_bit_alu_5 (
    .A(A[4]), .B(B[4]), .Select(Select), .Cin(n1_bit_alu_4_cout), .Result(Result[4]), .Cout(n1_bit_alu_5_cout));
  _1_Bit_ALU u_1_bit_alu_6 (
    .A(A[5]), .B(B[5]), .Select(Select), .Cin(n1_bit_alu_5_cout), .Result(Result[5]), .Cout(n1_bit_alu_6_cout));
  _1_Bit_ALU u_1_bit_alu_7 (
    .A(A[6]), .B(B[6]), .Select(Select), .Cin(n1_bit_alu_6_cout), .Result(Result[6]), .Cout(n1_bit_alu_7_cout));
  _1_Bit_ALU u_1_bit_alu_8 (
    .A(A[7]), .B(B[7]), .Select(Select), .Cin(n1_bit_alu_7_cout), .Result(Result[7]), .Cout(n1_bit_alu_8_cout));
  _1_Bit_ALU u_1_bit_alu_9 (
    .A(A[8]), .B(B[8]), .Select(Select), .Cin(n1_bit_alu_8_cout), .Result(Result[8]), .Cout(n1_bit_alu_9_cout));
  _1_Bit_ALU u_1_bit_alu_10 (
    .A(A[9]), .B(B[9]), .Select(Select), .Cin(n1_bit_alu_9_cout), .Result(Result[9]),
    .Cout(n1_bit_alu_10_cout));
  _1_Bit_ALU u_1_bit_alu_11 (
    .A(A[10]), .B(B[10]), .Select(Select), .Cin(n1_bit_alu_10_cout), .Result(Result[10]),
    .Cout(n1_bit_alu_11_cout));
  _1_Bit_ALU u_1_bit_alu_12 (
    .A(A[11]), .B(B[11]), .Select(Select), .Cin(n1_bit_alu_11_cout), .Result(Result[11]),
    .Cout(n1_bit_alu_12_cout));
  _1_Bit_ALU u_1_bit_alu_13 (
    .A(A[12]), .B(B[12]), .Select(Select), .Cin(n1_bit_alu_12_cout), .Result(Result[12]),
    .Cout(n1_bit_alu_13_cout));
  _1_Bit_ALU u_1_bit_alu_14 (
    .A(A[13]), .B(B[13]), .Select(Select), .Cin(n1_bit_alu_13_cout), .Result(Result[13]),
    .Cout(n1_bit_alu_14_cout));
  _1_Bit_ALU u_1_bit_alu_15 (
    .A(A[14]), .B(B[14]), .Select(Select), .Cin(n1_bit_alu_14_cout), .Result(Result[14]),
    .Cout(n1_bit_alu_15_cout));
  _1_Bit_ALU u_1_bit_alu_16 (
    .A(A[15]), .B(B[15]), .Select(Select), .Cin(n1_bit_alu_15_cout), .Result(Result[15]), .Cout(Cout));
endmodule

module Instruction_Fetch (
  input  Clock,
  input  Clear,
  output [15:0] out_3
);

  wire [1:0] adder_1_out, register_1_q;

  Register_part #(.width(2)) register_1 (.D(adder_1_out), .Q(register_1_q), .clk(Clock), .clr(Clear));  // open: en
  ROM #(.addrWidth(2), .dataWidth(16)) rom_1 (.addr(register_1_q), .data(out_3));  // open: sel
  Adder #(.width(2)) adder_1 (.a(register_1_q), .b(2'b01), .out(adder_1_out));  // open: cin, cout

  // Notes on the sheet:
  //   16 Bit ISA
  //   4 Instraction
  //   contents of rom_1 (hex, n*v repeats v):
  //   2678 3789
endmodule

module R_Type (
  input  Clock,
  input  Clear,
  input  RegWrite,
  output [15:0] out_4,
  output [15:0] out_5,
  output [15:0] out_6,
  output [15:0] out_7
);

  wire [1:0] bit_extender_1_out;

  Instruction_Fetch instruction_fetch_1 (.Clock(Clock), .Clear(Clear), .out_3(out_4));
  Bit_Extender #(.in_width(4), .out_width(2)) bit_extender_1 (.in(out_4[15:12]), .out(bit_extender_1_out));
  Register register_1 (
    .Write_Register_RD(out_4[3:0]), .Write_Data(out_7), .RegWrite(RegWrite), .Clock(Clock),
    .Read_Data_1(out_5), .Read_Data_2(out_6), .Read_Register_2_RT(out_4[7:4]),
    .Read_Register_1_RS(out_4[11:8]));
  _16_Bit_ALU u_16_bit_alu_1 (.Select(bit_extender_1_out), .A(out_5), .B(out_6), .Result(out_7));  // open: Cin, Cout

  // Notes on the sheet:
  //   OP | RS | RT | RD
  //   00 and, 01 Or, 10 add, 11 sub
endmodule

module I_Type (
  input  RegWrite,
  input  Clock,
  input  Clear,
  input  MemWrite,
  input  MemRead,
  output [15:0] out_6,
  output [15:0] out_7,
  output [1:0] out_8,
  output [15:0] out_9
);

  wire [1:0] adder_1_out, bit_extender_2_out, register_1_q;
  wire [15:0] bit_extender_1_out, n16_bit_alu_1_result, register_2_read_data_2;

  Register_part #(.width(2)) register_1 (.D(adder_1_out), .Q(register_1_q), .clk(Clock), .clr(Clear));  // open: en
  ROM #(.addrWidth(2), .dataWidth(16)) rom_1 (.addr(register_1_q), .data(out_7));  // open: sel
  Adder #(.width(2)) adder_1 (.a(register_1_q), .b(2'b01), .out(adder_1_out));  // open: cin, cout
  assign bit_extender_1_out = {{12{1'b0}}, out_7[3:0]};  // Bit_Extender bit_extender_1
  Bit_Extender #(.in_width(4), .out_width(2)) bit_extender_2 (.in(out_7[15:12]), .out(bit_extender_2_out));
  Register register_2 (
    .Write_Register_RD(out_7[7:4]), .Write_Data(out_9), .RegWrite(RegWrite), .Clock(Clock),
    .Read_Data_1(out_6), .Read_Data_2(register_2_read_data_2), .Read_Register_2_RT(out_7[7:4]),
    .Read_Register_1_RS(out_7[11:8]));
  _16_Bit_ALU u_16_bit_alu_1 (
    .Select(bit_extender_2_out), .A(bit_extender_1_out), .B(out_6), .Result(n16_bit_alu_1_result));  // open: Cin, Cout
  Bit_Extender #(.in_width(16), .out_width(2)) bit_extender_3 (.in(n16_bit_alu_1_result), .out(out_8));
  RAM #(.addrWidth(2), .dataWidth(16), .bus("separate")) ram_1 (
    .addr(out_8), .din(register_2_read_data_2), .data(out_9), .str(MemWrite), .clk(Clock), .ld(MemRead));  // open: sel, clr

  // Notes on the sheet:
  //   contents of rom_1 (hex, n*v repeats v):
  //   2061 2060
  //   OP|RD|Im|RS
  //   OP|RT|Im|RS
  //   OP | RS | RD | Im
  //   00 and, 01 Or, 10 add, 11 sub
  //   lw $t0, 1($zreo)     0010 0000 0110 0001     Hex-2061
  //   sw $t0, 0($zreo)     0010 0000 0110 0000     Hex-2060
endmodule
